// Digital circuit addressSpace.dig as structural Verilog
module addressSpace (
  input  C,
  input  [15:0] Ia,
  input  [15:0] Da,
  input  [15:0] Din,
  input  str,
  output [15:0] I,
  output [15:0] D
);

  wire and_1_out;
  wire [15:0] Data_d, ramdualport_1_d;

  and and_1 (and_1_out, str, Da[13]);
  ROM #(.AddrBits(13), .Bits(16)) Program (.A(Ia[12:0]), .sel(1'b1), .D(I));
  ROM #(.AddrBits(13), .Bits(16)) Data (.A(Da[12:0]), .sel(1'b1), .D(Data_d));
  RAMDualPort #(.AddrBits(13), .Bits(16)) ramdualport_1 (
    .A(Da[12:0]), .Din(Din), .str(and_1_out), .C(C), .ld(1'b1), .D(ramdualport_1_d));
  Multiplexer #(.Bits(16)) multiplexer_1 (.sel(Da[13]), .in_0(Data_d), .in_1(ramdualport_1_d), .out(D));

  // Other names for the same wires on the sheet: Data_High = Da[13]; Inst_High = Ia[13]

  // Notes on the sheet:
  //   contents of Program (hex, n*v repeats v):
  //   26,beef,440f
endmodule
