// Digital circuit alu.dig as structural Verilog
module alu (
  input  C,
  input  [15:0] a,
  input  [15:0] b,
  input  [3:0] op,
  input  en,
  output [15:0] out
);

  wire and_2_out, CarryLUT_d, xor_2_out;
  wire [0:0] add_1_c_o;
  wire [15:0] add_1_s, and_1_out, bitextender_1_out, bitextender_2_out, Carry_q, \cᵢ , \cₒ ,
       multiplexer_1_out, or_1_out, \shiftleft_1_cₒ , shiftleft_1_out, \shiftright_1_cₒ , shiftright_1_out,
       xor_1_out, xor_3_out;
  wire [31:0] mul_1_mul;

  BitExtender #(.inputBits(1)) bitextender_1 (.in(op[0]), .out(bitextender_1_out));
  BitExtender #(.inputBits(1)) bitextender_2 (.in(a[15]), .out(bitextender_2_out));
  assign xor_1_out = b ^ bitextender_1_out;  // XOr xor_1, 16 bits wide
  xor xor_2 (xor_2_out, \cᵢ [0], op[0]);
  Multiplexer #(.Bits(16)) multiplexer_1 (.sel(op[3]), .in_0(bitextender_2_out), .in_1(\cᵢ ), .out(multiplexer_1_out));
  shiftLeft shiftleft_1 (.in(a), .fill(\cᵢ ), .shift(b[3:0]), .out(shiftleft_1_out), .\cₒ (\shiftleft_1_cₒ ));
  shiftRight shiftright_1 (
    .in(a), .fill(multiplexer_1_out), .shift(b[3:0]), .out(shiftright_1_out), .\cₒ (\shiftright_1_cₒ ));
  Mul #(.Signed("true"), .Bits(16)) mul_1 (.a(a), .b(b), .mul(mul_1_mul));
  Add #(.Bits(16)) add_1 (.a(a), .b(xor_1_out), .c_i(xor_2_out), .s(add_1_s), .c_o(add_1_c_o[0]));
  assign or_1_out = a | b;  // Or or_1, 16 bits wide
  assign and_1_out = a & b;  // And and_1, 16 bits wide
  assign xor_3_out = a ^ b;  // XOr xor_3, 16 bits wide
  ROM #(.AddrBits(3)) CarryLUT (.A(op[2:0]), .sel(1'b1), .D(CarryLUT_d));
  and and_2 (and_2_out, CarryLUT_d, en);
  Register #(.Bits(16)) Carry (.D(\cₒ ), .C(C), .en(and_2_out), .Q(Carry_q));
  Multiplexer #(.Bits(16)) multiplexer_2 (.sel(op[3]), .in_0({16{1'b0}}), .in_1(Carry_q), .out(\cᵢ ));
  Multiplexer #(.Selector_Bits(3), .Bits(16)) multiplexer_3 (
    .sel(op[2:0]), .in_0({16{1'b0}}), .in_1({16{1'b0}}), .in_2({16{1'b0}}), .in_3(mul_1_mul[31:16]),
    .in_4({{15{1'b0}}, add_1_c_o[0]}), .in_5({{15{1'b0}}, add_1_c_o[0]}), .in_6(\shiftleft_1_cₒ ),
    .in_7(shiftright_1_out), .out(\cₒ ));
  Multiplexer #(.Selector_Bits(3), .Bits(16)) multiplexer_4 (
    .sel(op[2:0]), .in_0(or_1_out), .in_1(and_1_out), .in_2(xor_3_out), .in_3(mul_1_mul[15:0]),
    .in_4(add_1_s), .in_5(add_1_s), .in_6(shiftleft_1_out), .in_7(\shiftright_1_cₒ ), .out(out));

  // Other names for the same wires on the sheet: fun3[2:0] = op[2:0]; sub = op[0]; carry = op[3]

  // Notes on the sheet:
  //   Addition & Subtraction
  //   Shifting
  //   Control
  //   Bitwise Logic
  //   Multiplication
  //   contents of CarryLUT (hex, n*v repeats v):
  //   a,a,a,1,1,1,9,1
endmodule
