// Digital circuit canis.dig as structural Verilog
module canis (
  input  clk
);

  wire or_1_out, or_2_out, or_3_out;
  wire [1:0] instruction_p4_6;
  wire [2:0] instruction_p4;
  wire [3:0] instruction_p4_3;
  wire [4:0] instruction_p4_2, instruction_p4_4, instruction_p4_5;
  wire [15:0] add_1_s, PC_q, write_mode_q, write_reg_p4;
  wire [23:0] ram_1__2d;
  wire [31:24] ram_1__2d_2;

  or or_1 (or_1_out, 1'b1, or_2_out);
  interstageRegister #(.generic("bits := 16;")) PC (.C(clk), .D(add_1_s), .pass(or_1_out), .Q(PC_q));
  Add #(.Bits(16)) add_1 (.a(PC_q), .b(16'h1), .c_i(1'b0), .s(add_1_s));  // open: c_o
  ram #(.generic("addrBits := 16;")) ram_1 (
    .C(clk), ._1A({16{1'b0}}), ._1Din({32{1'b0}}), ._2A(PC_q), .we(1'b0), .am(2'b00), .sign(1'b0),
    ._2D({ram_1__2d_2, ram_1__2d}));  // open: _1D
  or or_2 (or_2_out, 1'b1, or_3_out);
  // interstageRegister #(.generic("bits := 24;")) instruction: pin names not known; wires that end beside it: clk, ram_1__2d, or_2_out, {instruction_p4_6, instruction_p4_5, instruction_p4_4, instruction_p4_3, instruction_p4_2, instruction_p4}, instruction_p4, instruction_p4_3, instruction_p4_6
  RegisterFile #(.AddrBits(5), .Bits(16)) Registers (
    .C(clk), .Ra(instruction_p4_4), .Rb(instruction_p4_5));  // open: Din, we, Rw, Da, Db
  or or_3 (or_3_out, 1'b1, 1'b1);
  // interstageRegister #(.generic("bits := 5;")) write_reg: pin names not known; wires that end beside it: clk, instruction_p4_2, or_3_out, write_reg_p4
  interstageRegister #(.generic("bits := 5;")) imm (.C(clk), .pass(or_3_out));  // open: D, Q
  interstageRegister #(.generic("bits := 16;")) ALU_a (.C(clk), .pass(or_3_out));  // open: D, Q
  interstageRegister #(.generic("bits := 16;")) ALU_b (.C(clk), .pass(or_3_out));  // open: D, Q
  interstageRegister #(.generic("bits := 6;")) ALU_op (.C(clk), .pass(or_3_out));  // open: D, Q
  interstageRegister #(.generic("bits := 2;")) write_mode (.C(clk), .pass(or_3_out), .Q(write_mode_q));  // open: D
  alu alu_1 ();  // open: a, b, op, C, out, cry
  interstageRegister #(.generic("bits := 5;")) write_reg_2 (.C(clk), .D(write_reg_p4), .pass(1'b1));  // open: Q
  interstageRegister #(.generic("bits := 16;")) write_A (.C(clk), .pass(1'b1));  // open: D, Q
  interstageRegister #(.generic("bits := 16;")) write_D (.C(clk), .pass(1'b1));  // open: D, Q
  interstageRegister #(.generic("bits := 2;")) write_mode_2 (.C(clk), .D(write_mode_q), .pass(1'b1));  // open: Q

  // Notes on the sheet:
  //   Fetch
  //   Decode
  //   Execute
  //   Store
endmodule
